# Fritzing sketch antena (saved by Fritzing 1.0.8)

parts:
  VCC1 = 18650 battery holder [package=battery-18650-kit]
  M1 = MT3608 Module
  M2 = TP4056 Module [part_number=HW-107]
  M3 = DOIT Esp32 DevKit v1 (30 pins long, 11 pins width) [part_number=ESP32S-PIN30]
  Chave_gangorra = SWITCH-SPST-2 [package=switch-spst-vertical]

nets:
  N1: VCC1.+, M2.BAT-
  N2: VCC1.-, M2.BAT+
  N3: M1.pin1, M2.OUT-#1
  N4: M1.pin2, M2.OUT-#4
  N5: M1.pin3, Chave_gangorra.O
  N6: M1.pin4, M3.GND
  N7: M3.VIN, Chave_gangorra.P

custom parts:
  18650 battery holder: 18650 Battery
  MT3608 Module: MT3608 Boost Converter Module Links: Aerosemi MT3608 2A Step Up Converter datasheet
  TP4056 Module: TP4056 Lithium Battery Charge Management Module Links: TP4056 website
  DOIT Esp32 DevKit v1 (30 pins long, 11 pins width): The DOIT Esp32 DevKit v1 is one of the development board created by DOIT to evaluate the ESP-WROOM-32 module. It is based on the ESP32 microcontroller that boasts Wifi, Bluetooth, Ethernet and Low Power support all in a single chip. (vanepp) made breadboard work, adjusted pin numbering and labels and reduced size of schematic and cleaned up pcb. This chip is 30pins long (2 x15) and 11 pins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
